// Logisim project Lab 4 Base.circ as structural Verilog: 3 circuits, main circuit register_file
module register_file (
  input  [7:0] data_write,
  input  clear,
  input  write_enable,
  input  [1:0] read_reg,
  input  [1:0] write_reg,
  input  clk,
  input  reset,
  output [7:0] data_read
);
endmodule

module alu (
  input  [7:0] A,
  input  [7:0] B,
  input  op,
  output [7:0] data_out
);
endmodule

module instr_decoder (
  input  [7:0] instr,
  output [1:0] imm,
  output [1:0] read_reg,
  output [1:0] write_reg,
  output write_en,
  output alu_op,
  output reg_clear
);
endmodule
